# Fritzing sketch PerfboardArduino (saved by Fritzing 0.8.3b)
circuit board: 16.9333cm x 5.64444cm
stripboards: 1

parts:
  U1 = atmega168 [package=dip]
  S1 = Pushbutton [package="[THT]"]
  R1 = Resistor [tolerance=±5% resistance=10k package=THT]
  LED1 = LED - 5mm [color="Red (633nm)" package="5 mm [THT]"]
  R2 = Resistor [tolerance=±5% resistance=220 package=THT]
  U2 = Voltage Regulator - 5V [package="TO220 [THT]"]
  C3 = Electrolytic Capacitor [capacitance=10µF package="100 mil [THT, electrolytic]"]
  C4 = Electrolytic Capacitor [capacitance=10µF package="100 mil [THT, electrolytic]"]
  C5 = Tantalum Capacitor [capacitance=22µF package="100 mil [THT, tantalum]"]
  C6 = Tantalum Capacitor [capacitance=22µF package="100 mil [THT, tantalum]"]
  XTAL1 = Crystal [frequency="16 Mhz" package=THT]

nets:
  N1: U1.RESET, S1.Pin_3, S1.Pin_4, R1.Pin_0
  N2: U1.VCC, U1.AVCC, U1.AREF, U2.output_voltage, C3.+
  N3: U1.GND#7, S1.Pin_1, S1.Pin_2, R1.Pin_1, R2.Pin_1, U2.GND, C3.-, C4.-, C5.-, C6.-
  N4: U1.XLAT1, C6.+, XTAL1.pin_0
  N5: U1.XLAT2, C5.+, XTAL1.pin_1
  N6: LED1.cathode, R2.Pin_0
  N7: U2.input_voltage, C4.+
