# Fritzing sketch adpcb (saved by Fritzing 0.8.3b)
circuit board: 3.06757cm x 5.12966cm
perfboards: 1

parts:
  ATMega16820PU = atmega168 [package=dip]
  7805 = Voltage Regulator - 5V [package="TO220 [THT]"]
  C1 = Electrolytic Capacitor [capacitance=10µF package="100 mil [THT, electrolytic]"]
  C2 = Electrolytic Capacitor [capacitance=10µF package="100 mil [THT, electrolytic]"]
  16MHz = Crystal [frequency="16 Mhz" package=THT]
  C4 = Tantalum Capacitor [capacitance=1nF package="100 mil [THT, tantalum]"]
  S1 = Pushbutton [package="[THT]"]
  J1 = female pin header, 5 pins [form="♀ (female)"]
  J2 = female pin header, 4 pins [form="♀ (female)"]
  R1 = Resistor [tolerance=±5% resistance=10k package=THT]
  R2 = Resistor [tolerance=±5% resistance=220 package=THT]
  LED = LED - 5mm [color="Red (633nm)" package="5 mm [THT]"]
  J3 = female pin header, 6 pins [form="♀ (female)"]
  J4 = female pin header, 5 pins [form="♀ (female)"]
  9V = male pin header, 2 pins [form="♂ (male)"]
  5V = female pin header, 2 pins [form="♀ (female)"]
  RST = female pin header, 1 pin [form="♀ (female)"]
  C3 = Tantalum Capacitor [capacitance="1 μF" package="100 mil [THT, tantalum]"]

nets:
  N1: ATMega16820PU.RESET, S1.Pin_3, S1.Pin_4, R1.Pin_0, RST.pin1
  N2: ATMega16820PU.D0_(RX), J1.pin1
  N3: ATMega16820PU.D1_(TX), J1.pin2
  N4: ATMega16820PU.D2, J1.pin3
  N5: ATMega16820PU.D3_(PWM), J1.pin4
  N6: ATMega16820PU.D4, J1.pin5
  N7: ATMega16820PU.VCC, ATMega16820PU.AVCC, ATMega16820PU.AREF, 7805.output_voltage, C1.+, R1.Pin_1, LED.anode
  GND: ATMega16820PU.GND, 7805.GND, C1.-, C2.-, C4.-, S1.Pin_1, S1.Pin_2, R2.Pin_0, 9V.pin2, 5V.pin2, C3.-
  N8: ATMega16820PU.XLAT1, 16MHz.pin_0, C3.+
  N9: ATMega16820PU.XLAT2, 16MHz.pin_1, C4.+
  N10: ATMega16820PU.D5_(PWM), J2.pin1
  N11: ATMega16820PU.D6_(PWM), J2.pin2
  N12: ATMega16820PU.D7, J2.pin3
  N13: ATMega16820PU.D8, J2.pin4
  N14: ATMega16820PU.D9_(PWM), J4.pin5
  N15: ATMega16820PU.D10_(PWM), J4.pin4
  N16: ATMega16820PU.D11_(PWM), J4.pin3
  N17: ATMega16820PU.D12, J4.pin2
  N18: ATMega16820PU.D13, J4.pin1
  N19: ATMega16820PU.A0, J3.pin6
  N20: ATMega16820PU.A1, J3.pin5
  N21: ATMega16820PU.A2, J3.pin4
  N22: ATMega16820PU.A3, J3.pin3
  N23: ATMega16820PU.A4, J3.pin2
  N24: ATMega16820PU.A5, J3.pin1
  N25: 7805.input_voltage, C2.+, 9V.pin1
  N26: R2.Pin_1, LED.cathode
